// Logisim project ULA.circ as structural Verilog: 19 circuits, main circuit ULA
module ULA (
  input  [7:0] Palavra_A,
  input  [7:0] Palavra_B,
  input  [3:0] \Operação ,
  output [15:0] out_4
);

  wire reset_out, slt_1_resultado;
  wire [2:0] comparador_8_bits_1_a_b;
  wire [7:0] and_1_resultado, divisor_1_resultado, not_1_resultado, or_1_resultado;
  wire [8:0] somador_8_bits_1_resultado, sub_8b_1_resultado;
  wire [15:0] multiplicador_1_resultado;

  Button reset (.out(reset_out));
  somador_8_bits somador_8_bits_1 (
    .Palavra_A(Palavra_A), .Palavra_B(Palavra_B), .Resultado(somador_8_bits_1_resultado));
  sub_8b sub_8b_1 (.Palavra_A(Palavra_A), .Palavra_B(Palavra_B), .Resultado(sub_8b_1_resultado));
  multiplicador multiplicador_1 (
    .Palavra_A(Palavra_A), .Palavra_B(Palavra_B), .reset(reset_out), .Resultado(multiplicador_1_resultado));
  divisor divisor_1 (.Palavra_A(Palavra_A), .Palavra_B(Palavra_B), .reset(reset_out), .Resultado(divisor_1_resultado));
  \and  and_1 (.Palavra_A(Palavra_A), .Palavra_B(Palavra_B), .Resultado(and_1_resultado));
  \or  or_1 (.Palavra_A(Palavra_A), .Palavra_B(Palavra_B), .Resultado(or_1_resultado));
  \not  not_1 (.Palavra_A(Palavra_A), .Resultado(not_1_resultado));
  comparador_8_bits comparador_8_bits_1 (
    .Palavra_A(Palavra_A), .Palavra_B(Palavra_B), .a_b(comparador_8_bits_1_a_b[0]),
    .a_b_2(comparador_8_bits_1_a_b[1]), .a_b_3(comparador_8_bits_1_a_b[2]));
  slt slt_1 (.Palavra_B(Palavra_A), .Palavra_A(Palavra_B), .Resultado(slt_1_resultado));
  controlador controlador_1 (
    .Somador(somador_8_bits_1_resultado), .Subtrator(sub_8b_1_resultado),
    .Multiplicador(multiplicador_1_resultado), .Divisor(divisor_1_resultado), .AND(and_1_resultado),
    .OR(or_1_resultado), .NOT(not_1_resultado), .Comparador(comparador_8_bits_1_a_b), .SLT(slt_1_resultado),
    .Select(\Operação ), .out_11(out_4));

  // Notes on the sheet:
  //   0000 - soma
  //   0001 - subtração
  //   0011 - divisão
  //   0100 - and
  //   0101 - or
  //   0111 - comparar
  //   1000 - slt
  //   0010 - multiplicação
  //   0110 - not (palavra A)
endmodule

// Som
module somador_completo (
  input  C,
  input  A,
  input  B,
  output R,
  output Carry
);

  wire and_1_out, and_2_out, xor_1_out, xor_2_out;

  xor xor_1 (xor_1_out, A, B);
  xor xor_2 (xor_2_out, A, B);
  xor xor_3 (R, xor_1_out, C);
  and and_1 (and_1_out, xor_2_out, C);
  or or_1 (Carry, and_1_out, and_2_out);
  and and_2 (and_2_out, A, B);
endmodule

// Sub
module subtrador_completo (
  input  Bin,
  input  A,
  input  B,
  output R,
  output Bout
);

  wire and_1_out, and_2_out, not_1_out, xor_1_out, xor_3_out;

  xor xor_1 (xor_1_out, A, B);
  xor xor_2 (R, xor_1_out, Bin);
  xor xor_3 (xor_3_out, B, Bin);
  and and_1 (and_1_out, xor_3_out, not_1_out);
  not not_1 (not_1_out, A);
  and and_2 (and_2_out, B, Bin);
  or or_1 (Bout, and_1_out, and_2_out);
endmodule

// Mult
module multiplicador (
  input  [7:0] Palavra_A,
  input  [7:0] Palavra_B,
  input  reset,
  output [15:0] Resultado
);

  wire and_1_out, clock_out, multiplexer_1_out, nand_1_out, not_1_out, not_2_out, not_3_out,
       somador_de_16_bits_1_r0, somador_de_16_bits_1_r1, somador_de_16_bits_1_r2, somador_de_16_bits_1_r3,
       somador_de_16_bits_1_r4, somador_de_16_bits_1_r5, somador_de_16_bits_1_r6, somador_de_16_bits_1_r7,
       somador_de_16_bits_1_r8, somador_de_16_bits_1_r9, somador_de_16_bits_1_r10, somador_de_16_bits_1_r11,
       somador_de_16_bits_1_r12, somador_de_16_bits_1_r13, somador_de_16_bits_1_r14, somador_de_16_bits_1_r15;
  wire [2:0] Contador_q_2;
  wire [3:3] Contador_q;
  wire [7:0] and_9_out;
  wire [15:0] shifter_1_out;

  Clock clock (.out(clock_out));
  and and_1 (and_1_out, clock_out, nand_1_out);
  memoria_16_bits memoria_16_bits_1 (
    .clock(and_1_out), .reset(reset), .E15(somador_de_16_bits_1_r15), .E14(somador_de_16_bits_1_r14),
    .E13(somador_de_16_bits_1_r13), .E12(somador_de_16_bits_1_r12), .E11(somador_de_16_bits_1_r11),
    .E10(somador_de_16_bits_1_r10), .E9(somador_de_16_bits_1_r9), .E8(somador_de_16_bits_1_r8),
    .E7(somador_de_16_bits_1_r7), .E6(somador_de_16_bits_1_r6), .E5(somador_de_16_bits_1_r5),
    .E4(somador_de_16_bits_1_r4), .E3(somador_de_16_bits_1_r3), .E2(somador_de_16_bits_1_r2),
    .E1(somador_de_16_bits_1_r1), .E0(somador_de_16_bits_1_r0), .S15(Resultado[15]), .S14(Resultado[14]),
    .S13(Resultado[13]), .S12(Resultado[12]), .S11(Resultado[11]), .S10(Resultado[10]), .S9(Resultado[9]),
    .S8(Resultado[8]), .S7(Resultado[7]), .S6(Resultado[6]), .S5(Resultado[5]), .S4(Resultado[4]),
    .S3(Resultado[3]), .S2(Resultado[2]), .S1(Resultado[1]), .S0(Resultado[0]));
  Counter #(.width(4), .max('hf)) Contador (
    .Q({Contador_q[3], Contador_q_2}), .clk(and_1_out), .clr(reset));  // open: load, D, count, carry
  not not_1 (not_1_out, Contador_q_2[2]);
  not not_2 (not_2_out, Contador_q_2[1]);
  nand nand_1 (nand_1_out, Contador_q[3], not_1_out, not_2_out, not_3_out);
  Multiplexer #(.select(3)) multiplexer_1 (
    .in0(Palavra_B[0]), .in1(Palavra_B[1]), .in2(Palavra_B[2]), .in3(Palavra_B[3]), .in4(Palavra_B[4]),
    .in5(Palavra_B[5]), .in6(Palavra_B[6]), .in7(Palavra_B[7]), .out(multiplexer_1_out), .sel(Contador_q_2),
    .en(1'b1));
  not not_3 (not_3_out, Contador_q_2[0]);
  and and_2 (and_9_out[6], Palavra_A[6], multiplexer_1_out);
  and and_3 (and_9_out[7], Palavra_A[7], multiplexer_1_out);
  and and_4 (and_9_out[4], Palavra_A[4], multiplexer_1_out);
  and and_5 (and_9_out[5], Palavra_A[5], multiplexer_1_out);
  somador_de_16_bits somador_de_16_bits_1 (
    .A15(Resultado[15]), .B15(shifter_1_out[15]), .A14(Resultado[14]), .B14(shifter_1_out[14]),
    .A13(Resultado[13]), .B13(shifter_1_out[13]), .A12(Resultado[12]), .B12(shifter_1_out[12]),
    .A11(Resultado[11]), .B11(shifter_1_out[11]), .A10(Resultado[10]), .B10(shifter_1_out[10]),
    .A9(Resultado[9]), .B9(shifter_1_out[9]), .A8(Resultado[8]), .B8(shifter_1_out[8]), .A7(Resultado[7]),
    .B7(shifter_1_out[7]), .A6(Resultado[6]), .B6(shifter_1_out[6]), .A5(Resultado[5]),
    .B5(shifter_1_out[5]), .A4(Resultado[4]), .B4(shifter_1_out[4]), .A3(Resultado[3]),
    .B3(shifter_1_out[3]), .A2(Resultado[2]), .B2(shifter_1_out[2]), .A1(Resultado[1]),
    .B1(shifter_1_out[1]), .A0(Resultado[0]), .B0(shifter_1_out[0]), .R15(somador_de_16_bits_1_r15),
    .R14(somador_de_16_bits_1_r14), .R13(somador_de_16_bits_1_r13), .R12(somador_de_16_bits_1_r12),
    .R11(somador_de_16_bits_1_r11), .R10(somador_de_16_bits_1_r10), .R9(somador_de_16_bits_1_r9),
    .R8(somador_de_16_bits_1_r8), .R7(somador_de_16_bits_1_r7), .R6(somador_de_16_bits_1_r6),
    .R5(somador_de_16_bits_1_r5), .R4(somador_de_16_bits_1_r4), .R3(somador_de_16_bits_1_r3),
    .R2(somador_de_16_bits_1_r2), .R1(somador_de_16_bits_1_r1), .R0(somador_de_16_bits_1_r0));  // open: C
  and and_6 (and_9_out[2], Palavra_A[2], multiplexer_1_out);
  and and_7 (and_9_out[3], Palavra_A[3], multiplexer_1_out);
  Shifter #(.width(16)) shifter_1 (
    .in({{8{1'b0}}, and_9_out}), .\dist ({Contador_q[3], Contador_q_2}), .out(shifter_1_out));
  and and_8 (and_9_out[1], Palavra_A[1], multiplexer_1_out);
  and and_9 (and_9_out[0], Palavra_A[0], multiplexer_1_out);

  // Notes on the sheet:
  //   Deslocador
endmodule

// som
module somador_8_bits (
  input  [7:0] Palavra_A,
  input  [7:0] Palavra_B,
  output [8:0] Resultado
);

  wire somador_completo_1_carry, somador_completo_3_carry, somador_completo_4_carry,
       somador_completo_5_carry, somador_completo_6_carry, somador_completo_7_carry, somador_completo_8_carry;

  somador_completo somador_completo_1 (
    .C(somador_completo_3_carry), .A(Palavra_A[6]), .B(Palavra_B[6]), .R(Resultado[6]),
    .Carry(somador_completo_1_carry));
  somador_completo somador_completo_2 (
    .C(somador_completo_1_carry), .A(Palavra_A[7]), .B(Palavra_B[7]), .R(Resultado[7]), .Carry(Resultado[8]));
  somador_completo somador_completo_3 (
    .C(somador_completo_4_carry), .A(Palavra_A[5]), .B(Palavra_B[5]), .R(Resultado[5]),
    .Carry(somador_completo_3_carry));
  somador_completo somador_completo_4 (
    .C(somador_completo_6_carry), .A(Palavra_A[4]), .B(Palavra_B[4]), .R(Resultado[4]),
    .Carry(somador_completo_4_carry));
  somador_completo somador_completo_5 (
    .C(somador_completo_7_carry), .A(Palavra_A[2]), .B(Palavra_B[2]), .R(Resultado[2]),
    .Carry(somador_completo_5_carry));
  somador_completo somador_completo_6 (
    .C(somador_completo_5_carry), .A(Palavra_A[3]), .B(Palavra_B[3]), .R(Resultado[3]),
    .Carry(somador_completo_6_carry));
  somador_completo somador_completo_7 (
    .C(somador_completo_8_carry), .A(Palavra_A[1]), .B(Palavra_B[1]), .R(Resultado[1]),
    .Carry(somador_completo_7_carry));
  somador_completo somador_completo_8 (
    .C(1'b0), .A(Palavra_A[0]), .B(Palavra_B[0]), .R(Resultado[0]), .Carry(somador_completo_8_carry));
endmodule

// Somador
module somador_de_16_bits (
  input  A15,
  input  B15,
  input  A14,
  input  B14,
  input  A13,
  input  B13,
  input  A12,
  input  B12,
  input  A11,
  input  B11,
  input  A10,
  input  B10,
  input  A9,
  input  B9,
  input  A8,
  input  B8,
  input  A7,
  input  B7,
  input  A6,
  input  B6,
  input  A5,
  input  B5,
  input  A4,
  input  B4,
  input  A3,
  input  B3,
  input  A2,
  input  B2,
  input  A1,
  input  B1,
  input  A0,
  input  B0,
  output C,
  output R15,
  output R14,
  output R13,
  output R12,
  output R11,
  output R10,
  output R9,
  output R8,
  output R7,
  output R6,
  output R5,
  output R4,
  output R3,
  output R2,
  output R1,
  output R0
);

  wire somador_completo_1_carry, somador_completo_3_carry, somador_completo_4_carry,
       somador_completo_5_carry, somador_completo_6_carry, somador_completo_7_carry,
       somador_completo_8_carry, somador_completo_9_carry, somador_completo_10_carry,
       somador_completo_11_carry, somador_completo_12_carry, somador_completo_13_carry,
       somador_completo_14_carry, somador_completo_15_carry, somador_completo_16_carry;

  somador_completo somador_completo_1 (
    .C(somador_completo_3_carry), .A(B14), .B(A14), .R(R14), .Carry(somador_completo_1_carry));
  somador_completo somador_completo_2 (.C(somador_completo_1_carry), .A(B15), .B(A15), .R(R15), .Carry(C));
  somador_completo somador_completo_3 (
    .C(somador_completo_4_carry), .A(B13), .B(A13), .R(R13), .Carry(somador_completo_3_carry));
  somador_completo somador_completo_4 (
    .C(somador_completo_6_carry), .A(B12), .B(A12), .R(R12), .Carry(somador_completo_4_carry));
  somador_completo somador_completo_5 (
    .C(somador_completo_7_carry), .A(B10), .B(A10), .R(R10), .Carry(somador_completo_5_carry));
  somador_completo somador_completo_6 (
    .C(somador_completo_5_carry), .A(B11), .B(A11), .R(R11), .Carry(somador_completo_6_carry));
  somador_completo somador_completo_7 (
    .C(somador_completo_8_carry), .A(B9), .B(A9), .R(R9), .Carry(somador_completo_7_carry));
  somador_completo somador_completo_8 (
    .C(somador_completo_10_carry), .A(B8), .B(A8), .R(R8), .Carry(somador_completo_8_carry));
  somador_completo somador_completo_9 (
    .C(somador_completo_11_carry), .A(B6), .B(A6), .R(R6), .Carry(somador_completo_9_carry));
  somador_completo somador_completo_10 (
    .C(somador_completo_9_carry), .A(B7), .B(A7), .R(R7), .Carry(somador_completo_10_carry));
  somador_completo somador_completo_11 (
    .C(somador_completo_12_carry), .A(B5), .B(A5), .R(R5), .Carry(somador_completo_11_carry));
  somador_completo somador_completo_12 (
    .C(somador_completo_13_carry), .A(B4), .B(A4), .R(R4), .Carry(somador_completo_12_carry));
  somador_completo somador_completo_13 (
    .C(somador_completo_14_carry), .A(B3), .B(A3), .R(R3), .Carry(somador_completo_13_carry));
  somador_completo somador_completo_14 (
    .C(somador_completo_15_carry), .A(B2), .B(A2), .R(R2), .Carry(somador_completo_14_carry));
  somador_completo somador_completo_15 (
    .C(somador_completo_16_carry), .A(B1), .B(A1), .R(R1), .Carry(somador_completo_15_carry));
  somador_completo somador_completo_16 (.C(1'b0), .A(B0), .B(A0), .R(R0), .Carry(somador_completo_16_carry));
endmodule

// Memória
module memoria_16_bits (
  input  E15,
  input  E14,
  input  E13,
  input  E12,
  input  E11,
  input  E10,
  input  E9,
  input  E8,
  input  E7,
  input  E6,
  input  E5,
  input  E4,
  input  E3,
  input  E2,
  input  E1,
  input  E0,
  input  clock,
  input  reset,
  output S15,
  output S14,
  output S13,
  output S12,
  output S11,
  output S10,
  output S9,
  output S8,
  output S7,
  output S6,
  output S5,
  output S4,
  output S3,
  output S2,
  output S1,
  output S0
);

  D_Flip_Flop d_ff_1 (.clk(clock), .D(E15), .Q(S15), .preset(1'b0), .en(1'b1), .reset(reset));  // open: Qn
  D_Flip_Flop d_ff_2 (.clk(clock), .D(E14), .Q(S14), .preset(1'b0), .en(1'b1), .reset(reset));  // open: Qn
  D_Flip_Flop d_ff_3 (.clk(clock), .D(E13), .Q(S13), .preset(1'b0), .en(1'b1), .reset(reset));  // open: Qn
  D_Flip_Flop d_ff_4 (.clk(clock), .D(E12), .Q(S12), .preset(1'b0), .en(1'b1), .reset(reset));  // open: Qn
  D_Flip_Flop d_ff_5 (.clk(clock), .D(E11), .Q(S11), .preset(1'b0), .en(1'b1), .reset(reset));  // open: Qn
  D_Flip_Flop d_ff_6 (.clk(clock), .D(E10), .Q(S10), .preset(1'b0), .en(1'b1), .reset(reset));  // open: Qn
  D_Flip_Flop d_ff_7 (.clk(clock), .D(E9), .Q(S9), .preset(1'b0), .en(1'b1), .reset(reset));  // open: Qn
  D_Flip_Flop d_ff_8 (.clk(clock), .D(E8), .Q(S8), .preset(1'b0), .en(1'b1), .reset(reset));  // open: Qn
  D_Flip_Flop d_ff_9 (.clk(clock), .D(E7), .Q(S7), .preset(1'b0), .en(1'b1), .reset(reset));  // open: Qn
  D_Flip_Flop d_ff_10 (.clk(clock), .D(E6), .Q(S6), .preset(1'b0), .en(1'b1), .reset(reset));  // open: Qn
  D_Flip_Flop d_ff_11 (.clk(clock), .D(E5), .Q(S5), .preset(1'b0), .en(1'b1), .reset(reset));  // open: Qn
  D_Flip_Flop d_ff_12 (.clk(clock), .D(E4), .Q(S4), .preset(1'b0), .en(1'b1), .reset(reset));  // open: Qn
  D_Flip_Flop d_ff_13 (.clk(clock), .D(E3), .Q(S3), .preset(1'b0), .en(1'b1), .reset(reset));  // open: Qn
  D_Flip_Flop d_ff_14 (.clk(clock), .D(E2), .Q(S2), .preset(1'b0), .en(1'b1), .reset(reset));  // open: Qn
  D_Flip_Flop d_ff_15 (.clk(clock), .D(E1), .Q(S1), .preset(1'b0), .en(1'b1), .reset(reset));  // open: Qn
  D_Flip_Flop d_ff_16 (.clk(clock), .D(E0), .Q(S0), .preset(1'b0), .en(1'b1), .reset(reset));  // open: Qn
endmodule

// Div
module divisor (
  input  [7:0] Palavra_A,
  input  [7:0] Palavra_B,
  input  reset,
  output [7:0] Resultado
);

  wire and_1_out, clock_out, memoria_8_bits_1_s0, memoria_8_bits_1_s1, memoria_8_bits_1_s2,
       memoria_8_bits_1_s3, memoria_8_bits_1_s4, memoria_8_bits_1_s5, memoria_8_bits_1_s6,
       memoria_8_bits_1_s7, multiplexer_1_out, multiplexer_2_out, multiplexer_3_out, multiplexer_4_out,
       multiplexer_5_out, multiplexer_6_out, multiplexer_7_out, multiplexer_8_out, nor_1_out, or_1_out,
       subtrator_8_bits_1_r0, subtrator_8_bits_1_r1, subtrator_8_bits_1_r2, subtrator_8_bits_1_r3,
       subtrator_8_bits_1_r4, subtrator_8_bits_1_r5, subtrator_8_bits_1_r6, subtrator_8_bits_1_r7;

  Clock clock (.out(clock_out));
  and and_1 (and_1_out, clock_out, or_1_out);
  Counter Contador (.Q(Resultado), .clk(and_1_out), .clr(reset));  // open: load, D, count, carry
  nor nor_1 (nor_1_out, Resultado[7], Resultado[6], Resultado[5], Resultado[4], Resultado[3], Resultado[2], Resultado[1], Resultado[0]);
  or or_1 (or_1_out, memoria_8_bits_1_s0, memoria_8_bits_1_s1, memoria_8_bits_1_s2, memoria_8_bits_1_s3, memoria_8_bits_1_s4, memoria_8_bits_1_s5, memoria_8_bits_1_s6, memoria_8_bits_1_s7);
  memoria_8_bits memoria_8_bits_1 (
    .clock(and_1_out), .reset(reset), .S7(memoria_8_bits_1_s7), .S6(memoria_8_bits_1_s6),
    .S5(memoria_8_bits_1_s5), .S4(memoria_8_bits_1_s4), .S3(memoria_8_bits_1_s3), .S2(memoria_8_bits_1_s2),
    .S1(memoria_8_bits_1_s1), .S0(memoria_8_bits_1_s0), .E7(subtrator_8_bits_1_r7),
    .E6(subtrator_8_bits_1_r6), .E5(subtrator_8_bits_1_r5), .E4(subtrator_8_bits_1_r4),
    .E3(subtrator_8_bits_1_r3), .E2(subtrator_8_bits_1_r2), .E1(subtrator_8_bits_1_r1),
    .E0(subtrator_8_bits_1_r0));
  Multiplexer multiplexer_1 (
    .in0(memoria_8_bits_1_s7), .in1(Palavra_A[7]), .out(multiplexer_1_out), .sel(nor_1_out), .en(1'b1));
  Multiplexer multiplexer_2 (
    .in0(memoria_8_bits_1_s6), .in1(Palavra_A[6]), .out(multiplexer_2_out), .sel(nor_1_out), .en(1'b1));
  Multiplexer multiplexer_3 (
    .in0(memoria_8_bits_1_s5), .in1(Palavra_A[5]), .out(multiplexer_3_out), .sel(nor_1_out), .en(1'b1));
  subtrator_8_bits subtrator_8_bits_1 (
    .A7(Palavra_B[7]), .B7(multiplexer_1_out), .A6(Palavra_B[6]), .B6(multiplexer_2_out), .A5(Palavra_B[5]),
    .B5(multiplexer_3_out), .A4(Palavra_B[4]), .B4(multiplexer_4_out), .A3(Palavra_B[3]),
    .B3(multiplexer_5_out), .A2(Palavra_B[2]), .B2(multiplexer_7_out), .A1(Palavra_B[1]),
    .B1(multiplexer_6_out), .A0(Palavra_B[0]), .B0(multiplexer_8_out), .R7(subtrator_8_bits_1_r7),
    .R6(subtrator_8_bits_1_r6), .R5(subtrator_8_bits_1_r5), .R4(subtrator_8_bits_1_r4),
    .R3(subtrator_8_bits_1_r3), .R2(subtrator_8_bits_1_r2), .R1(subtrator_8_bits_1_r1),
    .R0(subtrator_8_bits_1_r0));  // open: C
  Multiplexer multiplexer_4 (
    .in0(memoria_8_bits_1_s4), .in1(Palavra_A[4]), .out(multiplexer_4_out), .sel(nor_1_out), .en(1'b1));
  Multiplexer multiplexer_5 (
    .in0(memoria_8_bits_1_s3), .in1(Palavra_A[3]), .out(multiplexer_5_out), .sel(nor_1_out), .en(1'b1));
  Multiplexer multiplexer_6 (
    .in0(memoria_8_bits_1_s1), .in1(Palavra_A[1]), .out(multiplexer_6_out), .sel(nor_1_out), .en(1'b1));
  Multiplexer multiplexer_7 (
    .in0(memoria_8_bits_1_s2), .in1(Palavra_A[2]), .out(multiplexer_7_out), .sel(nor_1_out), .en(1'b1));
  Multiplexer multiplexer_8 (
    .in0(memoria_8_bits_1_s0), .in1(Palavra_A[0]), .out(multiplexer_8_out), .sel(nor_1_out), .en(1'b1));
endmodule

// Subtrator
module subtrator_8_bits (
  input  A7,
  input  B7,
  input  A6,
  input  B6,
  input  A5,
  input  B5,
  input  A4,
  input  B4,
  input  A3,
  input  B3,
  input  A2,
  input  B2,
  input  A1,
  input  B1,
  input  A0,
  input  B0,
  output C,
  output R7,
  output R6,
  output R5,
  output R4,
  output R3,
  output R2,
  output R1,
  output R0
);

  wire subtrador_completo_2_bout, subtrador_completo_3_bout, subtrador_completo_4_bout,
       subtrador_completo_5_bout, subtrador_completo_6_bout, subtrador_completo_7_bout,
       subtrador_completo_8_bout;

  subtrador_completo subtrador_completo_1 (.Bin(subtrador_completo_2_bout), .A(B7), .B(A7), .R(R7), .Bout(C));
  subtrador_completo subtrador_completo_2 (
    .Bin(subtrador_completo_3_bout), .A(B6), .B(A6), .R(R6), .Bout(subtrador_completo_2_bout));
  subtrador_completo subtrador_completo_3 (
    .Bin(subtrador_completo_4_bout), .A(B5), .B(A5), .R(R5), .Bout(subtrador_completo_3_bout));
  subtrador_completo subtrador_completo_4 (
    .Bin(subtrador_completo_6_bout), .A(B4), .B(A4), .R(R4), .Bout(subtrador_completo_4_bout));
  subtrador_completo subtrador_completo_5 (
    .Bin(subtrador_completo_7_bout), .A(B2), .B(A2), .R(R2), .Bout(subtrador_completo_5_bout));
  subtrador_completo subtrador_completo_6 (
    .Bin(subtrador_completo_5_bout), .A(B3), .B(A3), .R(R3), .Bout(subtrador_completo_6_bout));
  subtrador_completo subtrador_completo_7 (
    .Bin(subtrador_completo_8_bout), .A(B1), .B(A1), .R(R1), .Bout(subtrador_completo_7_bout));
  subtrador_completo subtrador_completo_8 (.Bin(1'b0), .A(B0), .B(A0), .R(R0), .Bout(subtrador_completo_8_bout));
endmodule

// Sub
module sub_8b (
  input  [7:0] Palavra_A,
  input  [7:0] Palavra_B,
  output [8:0] Resultado
);

  wire subtrador_completo_2_bout, subtrador_completo_3_bout, subtrador_completo_4_bout,
       subtrador_completo_5_bout, subtrador_completo_6_bout, subtrador_completo_7_bout,
       subtrador_completo_8_bout;

  subtrador_completo subtrador_completo_1 (
    .Bin(subtrador_completo_2_bout), .A(Palavra_A[7]), .B(Palavra_B[7]), .R(Resultado[7]), .Bout(Resultado[8]));
  subtrador_completo subtrador_completo_2 (
    .Bin(subtrador_completo_3_bout), .A(Palavra_A[6]), .B(Palavra_B[6]), .R(Resultado[6]),
    .Bout(subtrador_completo_2_bout));
  subtrador_completo subtrador_completo_3 (
    .Bin(subtrador_completo_4_bout), .A(Palavra_A[5]), .B(Palavra_B[5]), .R(Resultado[5]),
    .Bout(subtrador_completo_3_bout));
  subtrador_completo subtrador_completo_4 (
    .Bin(subtrador_completo_5_bout), .A(Palavra_A[4]), .B(Palavra_B[4]), .R(Resultado[4]),
    .Bout(subtrador_completo_4_bout));
  subtrador_completo subtrador_completo_5 (
    .Bin(subtrador_completo_6_bout), .A(Palavra_A[3]), .B(Palavra_B[3]), .R(Resultado[3]),
    .Bout(subtrador_completo_5_bout));
  subtrador_completo subtrador_completo_6 (
    .Bin(subtrador_completo_7_bout), .A(Palavra_A[2]), .B(Palavra_B[2]), .R(Resultado[2]),
    .Bout(subtrador_completo_6_bout));
  subtrador_completo subtrador_completo_7 (
    .Bin(subtrador_completo_8_bout), .A(Palavra_A[1]), .B(Palavra_B[1]), .R(Resultado[1]),
    .Bout(subtrador_completo_7_bout));
  subtrador_completo subtrador_completo_8 (
    .Bin(1'b0), .A(Palavra_A[0]), .B(Palavra_B[0]), .R(Resultado[0]), .Bout(subtrador_completo_8_bout));
endmodule

module memoria_8_bits (
  input  clock,
  input  reset,
  input  E7,
  input  E6,
  input  E5,
  input  E4,
  input  E3,
  input  E2,
  input  E1,
  input  E0,
  output S7,
  output S6,
  output S5,
  output S4,
  output S3,
  output S2,
  output S1,
  output S0
);

  D_Flip_Flop d_ff_1 (.clk(clock), .D(E7), .Q(S7), .preset(reset), .en(1'b1), .reset(1'b0));  // open: Qn
  D_Flip_Flop d_ff_2 (.clk(clock), .D(E6), .Q(S6), .preset(reset), .en(1'b1), .reset(1'b0));  // open: Qn
  D_Flip_Flop d_ff_3 (.clk(clock), .D(E5), .Q(S5), .preset(reset), .en(1'b1), .reset(1'b0));  // open: Qn
  D_Flip_Flop d_ff_4 (.clk(clock), .D(E4), .Q(S4), .preset(reset), .en(1'b1), .reset(1'b0));  // open: Qn
  D_Flip_Flop d_ff_5 (.clk(clock), .D(E3), .Q(S3), .preset(reset), .en(1'b1), .reset(1'b0));  // open: Qn
  D_Flip_Flop d_ff_6 (.clk(clock), .D(E2), .Q(S2), .preset(reset), .en(1'b1), .reset(1'b0));  // open: Qn
  D_Flip_Flop d_ff_7 (.clk(clock), .D(E0), .Q(S0), .preset(reset), .en(1'b1), .reset(1'b0));  // open: Qn
  D_Flip_Flop d_ff_8 (.clk(clock), .D(E1), .Q(S1), .preset(reset), .en(1'b1), .reset(1'b0));  // open: Qn
endmodule

// AND
module \and  (
  input  [7:0] Palavra_A,
  input  [7:0] Palavra_B,
  output [7:0] Resultado
);

  and and_1 (Resultado[0], Palavra_B[0], Palavra_A[0]);
  and and_2 (Resultado[1], Palavra_B[1], Palavra_A[1]);
  and and_3 (Resultado[2], Palavra_B[2], Palavra_A[2]);
  and and_4 (Resultado[3], Palavra_B[3], Palavra_A[3]);
  and and_5 (Resultado[4], Palavra_B[4], Palavra_A[4]);
  and and_6 (Resultado[5], Palavra_B[5], Palavra_A[5]);
  and and_7 (Resultado[6], Palavra_B[6], Palavra_A[6]);
  and and_8 (Resultado[7], Palavra_B[7], Palavra_A[7]);
endmodule

// OR
module \or  (
  input  [7:0] Palavra_A,
  input  [7:0] Palavra_B,
  output [7:0] Resultado
);

  or or_1 (Resultado[0], Palavra_B[0], Palavra_A[0]);
  or or_2 (Resultado[1], Palavra_B[1], Palavra_A[1]);
  or or_3 (Resultado[2], Palavra_B[2], Palavra_A[2]);
  or or_4 (Resultado[3], Palavra_B[3], Palavra_A[3]);
  or or_5 (Resultado[4], Palavra_B[4], Palavra_A[4]);
  or or_6 (Resultado[5], Palavra_B[5], Palavra_A[5]);
  or or_7 (Resultado[6], Palavra_B[6], Palavra_A[6]);
  or or_8 (Resultado[7], Palavra_B[7], Palavra_A[7]);
endmodule

// SLT
module slt (
  input  [7:0] Palavra_B,
  input  [7:0] Palavra_A,
  output Resultado
);

  subtrator_8_bits subtrator_8_bits_1 (
    .A7(Palavra_A[7]), .B7(Palavra_B[7]), .A6(Palavra_A[6]), .B6(Palavra_B[6]), .A5(Palavra_A[5]),
    .B5(Palavra_B[5]), .A4(Palavra_A[4]), .B4(Palavra_B[4]), .A3(Palavra_A[3]), .B3(Palavra_B[3]),
    .A2(Palavra_A[2]), .B2(Palavra_B[2]), .A1(Palavra_A[1]), .B1(Palavra_B[1]), .A0(Palavra_A[0]),
    .B0(Palavra_B[0]), .C(Resultado));  // open: R7, R6, R5, R4, R3, R2, R1, R0
endmodule

// NOT
module \not  (
  input  [7:0] Palavra_A,
  output [7:0] Resultado
);

  not not_1 (Resultado[7], Palavra_A[7]);
  not not_2 (Resultado[0], Palavra_A[0]);
  not not_3 (Resultado[5], Palavra_A[5]);
  not not_4 (Resultado[3], Palavra_A[3]);
  not not_5 (Resultado[4], Palavra_A[4]);
  not not_6 (Resultado[1], Palavra_A[1]);
  not not_7 (Resultado[6], Palavra_A[6]);
  not not_8 (Resultado[2], Palavra_A[2]);
endmodule

// comp
module comparador (
  input  xi,
  input  yi,
  input  zi,
  input  a,
  input  b,
  output xo,
  output yo,
  output zo
);

  wire and_1_out, and_3_out, not_1_out, not_2_out, xnor_1_out;

  not not_1 (not_1_out, a);
  not not_2 (not_2_out, b);
  and and_1 (and_1_out, yi, not_1_out, b);
  and and_2 (yo, yi, xnor_1_out);
  xnor xnor_1 (xnor_1_out, a, b);
  and and_3 (and_3_out, yi, a, not_2_out);
  or or_1 (xo, xi, and_1_out);
  or or_2 (zo, zi, and_3_out);
endmodule

// comp
module comparador_8_bits (
  input  [7:0] Palavra_A,
  input  [7:0] Palavra_B,
  output a_b,
  output a_b_2,
  output a_b_3
);

  wire comparador_1_xo, comparador_1_yo, comparador_1_zo, comparador_2_xo, comparador_2_yo, comparador_2_zo,
       comparador_3_xo, comparador_3_yo, comparador_3_zo, comparador_4_xo, comparador_4_yo, comparador_4_zo,
       comparador_5_xo, comparador_5_yo, comparador_5_zo, comparador_6_xo, comparador_6_yo, comparador_6_zo,
       comparador_7_xo, comparador_7_yo, comparador_7_zo;

  comparador comparador_1 (
    .a(Palavra_B[7]), .b(Palavra_A[7]), .xi(1'b0), .yi(1'b1), .zi(1'b0), .xo(comparador_1_xo),
    .yo(comparador_1_yo), .zo(comparador_1_zo));
  comparador comparador_2 (
    .a(Palavra_B[6]), .b(Palavra_A[6]), .xi(comparador_1_xo), .yi(comparador_1_yo), .zi(comparador_1_zo),
    .xo(comparador_2_xo), .yo(comparador_2_yo), .zo(comparador_2_zo));
  comparador comparador_3 (
    .a(Palavra_B[5]), .b(Palavra_A[5]), .xi(comparador_2_xo), .yi(comparador_2_yo), .zi(comparador_2_zo),
    .xo(comparador_3_xo), .yo(comparador_3_yo), .zo(comparador_3_zo));
  comparador comparador_4 (
    .a(Palavra_B[4]), .b(Palavra_A[4]), .xi(comparador_3_xo), .yi(comparador_3_yo), .zi(comparador_3_zo),
    .xo(comparador_4_xo), .yo(comparador_4_yo), .zo(comparador_4_zo));
  comparador comparador_5 (
    .a(Palavra_B[3]), .b(Palavra_A[3]), .xi(comparador_4_xo), .yi(comparador_4_yo), .zi(comparador_4_zo),
    .xo(comparador_5_xo), .yo(comparador_5_yo), .zo(comparador_5_zo));
  comparador comparador_6 (
    .a(Palavra_B[2]), .b(Palavra_A[2]), .xi(comparador_5_xo), .yi(comparador_5_yo), .zi(comparador_5_zo),
    .xo(comparador_6_xo), .yo(comparador_6_yo), .zo(comparador_6_zo));
  comparador comparador_7 (
    .a(Palavra_B[1]), .b(Palavra_A[1]), .xi(comparador_6_xo), .yi(comparador_6_yo), .zi(comparador_6_zo),
    .xo(comparador_7_xo), .yo(comparador_7_yo), .zo(comparador_7_zo));
  comparador comparador_8 (
    .a(Palavra_B[0]), .b(Palavra_A[0]), .xi(comparador_7_xo), .yi(comparador_7_yo), .zi(comparador_7_zo),
    .xo(a_b_3), .yo(a_b_2), .zo(a_b));
endmodule

module controlador (
  input  [3:0] Select,
  input  [8:0] Somador,
  input  [8:0] Subtrator,
  input  [15:0] Multiplicador,
  input  [7:0] Divisor,
  input  [7:0] AND,
  input  [7:0] OR,
  input  [7:0] NOT,
  input  [2:0] Comparador,
  input  SLT,
  output [15:0] out_11
);

  wire and_1_out, and_2_out, multiplexer_9_out, nor_1_out, not_1_out, not_2_out;
  wire [15:0] multiplexer_1_out;

  Multiplexer #(.select(3), .enable("false")) multiplexer_1 (
    .in0(Somador[0]), .in1(Subtrator[0]), .in2(Multiplicador[0]), .in3(Divisor[0]), .in4(AND[0]),
    .in5(OR[0]), .in6(NOT[0]), .in7(Comparador[0]), .out(multiplexer_1_out[0]), .sel(Select[2:0]));
  Multiplexer #(.select(3), .enable("false")) multiplexer_2 (
    .in0(Somador[1]), .in1(Subtrator[1]), .in2(Multiplicador[1]), .in3(Divisor[1]), .in4(AND[1]),
    .in5(OR[1]), .in6(NOT[1]), .in7(Comparador[1]), .out(multiplexer_1_out[1]), .sel(Select[2:0]));
  Multiplexer #(.select(3), .enable("false")) multiplexer_3 (
    .in0(Somador[2]), .in1(Subtrator[2]), .in2(Multiplicador[2]), .in3(Divisor[2]), .in4(AND[2]),
    .in5(OR[2]), .in6(NOT[2]), .in7(Comparador[2]), .out(multiplexer_1_out[2]), .sel(Select[2:0]));
  Multiplexer #(.select(3), .enable("false")) multiplexer_4 (
    .in0(Somador[3]), .in1(Subtrator[3]), .in2(Multiplicador[3]), .in3(Divisor[3]), .in4(AND[3]),
    .in5(OR[3]), .in6(NOT[3]), .in7(1'b0), .out(multiplexer_1_out[3]), .sel(Select[2:0]));
  Multiplexer #(.select(3), .enable("false")) multiplexer_5 (
    .in0(Somador[4]), .in1(Subtrator[4]), .in2(Multiplicador[4]), .in3(Divisor[4]), .in4(AND[4]),
    .in5(OR[4]), .in6(NOT[4]), .in7(1'b0), .out(multiplexer_1_out[4]), .sel(Select[2:0]));
  Multiplexer #(.select(3), .enable("false")) multiplexer_6 (
    .in0(Somador[5]), .in1(Subtrator[5]), .in2(Multiplicador[5]), .in3(Divisor[5]), .in4(AND[5]),
    .in5(OR[5]), .in6(NOT[5]), .in7(1'b0), .out(multiplexer_1_out[5]), .sel(Select[2:0]));
  Multiplexer #(.select(3), .enable("false")) multiplexer_7 (
    .in0(Somador[6]), .in1(Subtrator[6]), .in2(Multiplicador[6]), .in3(Divisor[6]), .in4(AND[6]),
    .in5(OR[6]), .in6(NOT[6]), .in7(1'b0), .out(multiplexer_1_out[6]), .sel(Select[2:0]));
  Multiplexer #(.select(3), .enable("false")) multiplexer_8 (
    .in0(Somador[7]), .in1(Subtrator[7]), .in2(Multiplicador[7]), .in3(Divisor[7]), .in4(AND[7]),
    .in5(OR[7]), .in6(NOT[7]), .in7(1'b0), .out(multiplexer_1_out[7]), .sel(Select[2:0]));
  Multiplexer #(.select(2), .enable("false")) multiplexer_9 (
    .in0(Somador[8]), .in1(Subtrator[8]), .in2(Multiplicador[8]), .out(multiplexer_9_out), .sel(Select[1:0]));  // open: in3
  not not_1 (not_1_out, Select[2]);
  not not_2 (not_2_out, Select[0]);
  and and_1 (and_1_out, Select[1], Select[0]);
  aux_controlador aux_controlador_1 (
    .in_2(Multiplicador[9]), .in_3(Multiplicador[10]), .in_4(Multiplicador[11]), .in_5(Multiplicador[12]),
    .in_6(Multiplicador[13]), .in_7(Multiplicador[14]), .in_8(Multiplicador[15]), .controle(and_2_out),
    .out_9(multiplexer_1_out[9]), .out_10(multiplexer_1_out[10]), .out_11(multiplexer_1_out[11]),
    .out_12(multiplexer_1_out[12]), .out_13(multiplexer_1_out[13]), .out_14(multiplexer_1_out[14]),
    .out_15(multiplexer_1_out[15]));
  and and_2 (and_2_out, not_1_out, Select[1], not_2_out);
  nor nor_1 (nor_1_out, and_1_out, Select[2]);
  and and_3 (multiplexer_1_out[8], nor_1_out, multiplexer_9_out);
  Multiplexer #(.width(16), .enable("false")) multiplexer_10 (
    .in0(multiplexer_1_out), .in1({{15{1'b0}}, SLT}), .out(out_11), .sel(Select[3]));
endmodule

// ctrl 7 bit
module aux_controlador (
  input  controle,
  input  in_2,
  input  in_3,
  input  in_4,
  input  in_5,
  input  in_6,
  input  in_7,
  input  in_8,
  output out_9,
  output out_10,
  output out_11,
  output out_12,
  output out_13,
  output out_14,
  output out_15
);

  and and_1 (out_9, in_2, controle);
  and and_2 (out_10, in_3, controle);
  and and_3 (out_11, in_4, controle);
  and and_4 (out_12, in_5, controle);
  and and_5 (out_13, in_6, controle);
  and and_6 (out_14, in_7, controle);
  and and_7 (out_15, in_8, controle);
endmodule
